# Fritzing sketch Circuit (saved by Fritzing 0.9.5d)

parts:
  Raspberry_Pi_1 = Raspberry Pi 3 [part_number=RPI-3-V1.2]
  Part1 = DHT22 module

nets:
  GND: Raspberry_Pi_1.GND, Part1.GND
  N1: Raspberry_Pi_1.GIPO21, Part1.DATA
  5V: Raspberry_Pi_1.5V, Part1.VCC
